// Logisim project 4_bit_adder.circ as structural Verilog: 6 circuits, main circuit main
module main (
  input  in_1,
  input  in_2,
  input  in_3,
  input  in_4,
  input  in_5,
  output out_6,
  output out_7,
  output out_8
);

  _2_bit_adder u_2_bit_adder_1 (
    .out_6(out_6), .in_1(in_1), .in_2(in_2), .in_3(in_3), .in_4(in_4), .out_7(out_7), .out_8(out_8),
    .in_5(in_5));
endmodule

module half_adder (
  input  in_1,
  input  in_2,
  output out_3,
  output out_4
);

  xor xor_1 (out_3, in_1, in_2);
  and and_1 (out_4, in_1, in_2);
endmodule

module full_adder (
  input  in_1,
  input  in_2,
  input  in_3,
  output out_4,
  output out_5
);

  wire half_adder_1_out_3, half_adder_1_out_4, half_adder_2_out_4;

  half_adder half_adder_1 (.in_1(in_2), .in_2(in_3), .out_3(half_adder_1_out_3), .out_4(half_adder_1_out_4));
  half_adder half_adder_2 (.in_1(in_1), .in_2(half_adder_1_out_3), .out_3(out_4), .out_4(half_adder_2_out_4));
  or or_1 (out_5, half_adder_2_out_4, half_adder_1_out_4);
endmodule

module _2_bit_adder (
  input  in_1,
  input  in_2,
  input  in_3,
  input  in_4,
  input  in_5,
  output out_6,
  output out_7,
  output out_8
);

  wire full_adder_2_out_5;

  full_adder full_adder_1 (.in_1(full_adder_2_out_5), .in_2(in_1), .in_3(in_3), .out_4(out_7), .out_5(out_6));
  full_adder full_adder_2 (.in_1(in_5), .in_2(in_2), .in_3(in_4), .out_4(out_8), .out_5(full_adder_2_out_5));
endmodule

module _4_bit_adder (
  input  in_1,
  input  in_2,
  input  in_3,
  input  in_4,
  input  in_5,
  input  in_6,
  input  in_7,
  input  in_8,
  input  in_9
);

  wire n2_bit_adder_2_out_6;

  _2_bit_adder u_2_bit_adder_1 (.in_5(n2_bit_adder_2_out_6));  // open: out_6, in_1, in_2, in_3, in_4, out_7, out_8
  _2_bit_adder u_2_bit_adder_2 (
    .out_6(n2_bit_adder_2_out_6), .in_1(in_8), .in_5(in_9));  // open: in_2, in_3, in_4, out_7, out_8
endmodule

module _4_bit_with_splitters (
  input  [3:0] in_1,
  input  [3:0] in_2,
  input  in_3,
  output out_4,
  output [3:0] out_5
);

  wire full_adder_2_out_5, full_adder_3_out_5, full_adder_4_out_5;

  full_adder full_adder_1 (.in_1(full_adder_2_out_5), .in_2(in_2[3]), .in_3(in_1[3]), .out_4(out_5[3]), .out_5(out_4));
  full_adder full_adder_2 (
    .in_1(full_adder_3_out_5), .in_2(in_2[2]), .in_3(in_1[2]), .out_4(out_5[2]), .out_5(full_adder_2_out_5));
  full_adder full_adder_3 (
    .in_1(full_adder_4_out_5), .in_2(in_2[1]), .in_3(in_1[1]), .out_4(out_5[1]), .out_5(full_adder_3_out_5));
  full_adder full_adder_4 (.in_1(in_3), .in_2(in_2[0]), .in_3(in_1[0]), .out_4(out_5[0]), .out_5(full_adder_4_out_5));
endmodule
