// Logisim project 8_bit_adder.circ as structural Verilog: 4 circuits, main circuit main
module main (
  input  [7:0] in_1,
  input  [7:0] in_2,
  input  in_3,
  input  in_4,
  input  in_5,
  output [7:0] out_6
);

  wire n8_bit_adder_1_out_18, ones_complement_1_out_10, ones_complement_1_out_11, ones_complement_1_out_12,
       ones_complement_1_out_13, ones_complement_1_out_14, ones_complement_1_out_15,
       ones_complement_1_out_16, ones_complement_1_out_17;

  // XOR_Gate xor_1 has open pins: in0=n8_bit_adder_1_out_18, in1=in_5, out=open
  ones_complement ones_complement_1 (
    .in_9(in_3), .in_1(in_2[7]), .in_2(in_2[6]), .in_3(in_2[5]), .in_4(in_2[4]), .in_5(in_2[3]),
    .in_6(in_2[2]), .in_7(in_2[1]), .in_8(in_2[0]), .out_10(ones_complement_1_out_10),
    .out_11(ones_complement_1_out_11), .out_12(ones_complement_1_out_12), .out_13(ones_complement_1_out_13),
    .out_14(ones_complement_1_out_14), .out_15(ones_complement_1_out_15), .out_16(ones_complement_1_out_16),
    .out_17(ones_complement_1_out_17));
  _8_bit_adder u_8_bit_adder_1 (
    .in_1(in_1[7]), .in_2(in_1[6]), .in_3(in_1[5]), .in_4(in_1[4]), .in_5(in_1[3]), .in_6(in_1[2]),
    .in_7(in_1[1]), .in_8(in_1[0]), .in_9(ones_complement_1_out_10), .in_10(ones_complement_1_out_11),
    .in_11(ones_complement_1_out_12), .in_12(ones_complement_1_out_13), .in_13(ones_complement_1_out_14),
    .in_14(ones_complement_1_out_15), .in_15(ones_complement_1_out_16), .in_16(ones_complement_1_out_17),
    .out_18(n8_bit_adder_1_out_18), .out_19(out_6[7]), .out_20(out_6[6]), .out_21(out_6[5]),
    .out_22(out_6[4]), .out_23(out_6[3]), .out_24(out_6[2]), .out_25(out_6[1]), .out_26(out_6[0]),
    .in_17(in_4));
endmodule

module _8_bit_adder (
  input  in_1,
  input  in_2,
  input  in_3,
  input  in_4,
  input  in_5,
  input  in_6,
  input  in_7,
  input  in_8,
  input  in_9,
  input  in_10,
  input  in_11,
  input  in_12,
  input  in_13,
  input  in_14,
  input  in_15,
  input  in_16,
  input  in_17,
  output out_18,
  output out_19,
  output out_20,
  output out_21,
  output out_22,
  output out_23,
  output out_24,
  output out_25,
  output out_26
);

  wire full_adder_1_out_5, full_adder_3_out_5, full_adder_4_out_5, full_adder_5_out_5, full_adder_6_out_5,
       full_adder_7_out_5, full_adder_8_out_5;

  full_adder full_adder_1 (
    .in_1(full_adder_3_out_5), .in_2(in_2), .in_3(in_10), .out_4(out_20), .out_5(full_adder_1_out_5));
  full_adder full_adder_2 (.in_1(full_adder_1_out_5), .in_2(in_1), .in_3(in_9), .out_4(out_19), .out_5(out_18));
  full_adder full_adder_3 (
    .in_1(full_adder_4_out_5), .in_2(in_3), .in_3(in_11), .out_4(out_21), .out_5(full_adder_3_out_5));
  full_adder full_adder_4 (
    .in_1(full_adder_6_out_5), .in_2(in_4), .in_3(in_12), .out_4(out_22), .out_5(full_adder_4_out_5));
  full_adder full_adder_5 (
    .in_1(full_adder_7_out_5), .in_2(in_6), .in_3(in_14), .out_4(out_24), .out_5(full_adder_5_out_5));
  full_adder full_adder_6 (
    .in_1(full_adder_5_out_5), .in_2(in_5), .in_3(in_13), .out_4(out_23), .out_5(full_adder_6_out_5));
  full_adder full_adder_7 (
    .in_1(full_adder_8_out_5), .in_2(in_7), .in_3(in_15), .out_4(out_25), .out_5(full_adder_7_out_5));
  full_adder full_adder_8 (.in_1(in_17), .in_2(in_8), .in_3(in_16), .out_4(out_26), .out_5(full_adder_8_out_5));
endmodule

module ones_complement (
  input  in_1,
  input  in_2,
  input  in_3,
  input  in_4,
  input  in_5,
  input  in_6,
  input  in_7,
  input  in_8,
  input  in_9,
  output out_10,
  output out_11,
  output out_12,
  output out_13,
  output out_14,
  output out_15,
  output out_16,
  output out_17
);

  wire controlled_inverter_1_out;

  assign controlled_inverter_1_out = 1'b1 ? ~in_9 : 1'bz;  // Controlled_Inverter controlled_inverter_1
  xor xor_1 (out_10, controlled_inverter_1_out, in_1);
  xor xor_2 (out_11, controlled_inverter_1_out, in_2);
  xor xor_3 (out_12, controlled_inverter_1_out, in_3);
  xor xor_4 (out_13, controlled_inverter_1_out, in_4);
  xor xor_5 (out_14, controlled_inverter_1_out, in_5);
  xor xor_6 (out_15, controlled_inverter_1_out, in_6);
  xor xor_7 (out_16, controlled_inverter_1_out, in_7);
  xor xor_8 (out_17, controlled_inverter_1_out, in_8);
endmodule

module latch (
  input  in_1,
  input  in_2,
  input  in_3,
  output out_4,
  output out_5
);

  wire and_1_out, and_2_out;

  and and_1 (and_1_out, in_1, in_2);
  and and_2 (and_2_out, in_2, in_3);
  nor nor_1 (out_4, and_1_out, out_5);
  nor nor_2 (out_5, out_4, and_2_out);
endmodule
