// Digital circuit latch.dig as structural Verilog
module latch (
  input  Data,
  input  Clock,
  output Q,
  output Q_Bar
);

  wire and_1_out, and_2_out, not_1_out;

  not not_1 (not_1_out, Data);
  and and_1 (and_1_out, not_1_out, Clock);
  and and_2 (and_2_out, Clock, Data);
  nor nor_1 (Q, and_1_out, Q_Bar);
  nor nor_2 (Q_Bar, Q, and_2_out);
endmodule
