// Digital circuit edge_triggered_d_flipflop.dig as structural Verilog
module edge_triggered_d_flipflop (
  input  A,
  input  B,
  output Y,
  output X
);

  wire and_1_out, and_2_out, and_3_out, and_4_out, nor_1_out, nor_2_out, not_1_out, not_2_out;

  not not_1 (not_1_out, B);
  not not_2 (not_2_out, A);
  and and_1 (and_1_out, A, not_1_out);
  and and_2 (and_2_out, not_1_out, not_2_out);
  nor nor_1 (nor_1_out, and_1_out, nor_2_out);
  nor nor_2 (nor_2_out, nor_1_out, and_2_out);
  and and_3 (and_3_out, nor_1_out, B);
  and and_4 (and_4_out, B, nor_2_out);
  nor nor_3 (Y, and_3_out, X);
  nor nor_4 (X, Y, and_4_out);
endmodule
